// Logisim project dz5.circ as structural Verilog: 4 circuits, main circuit dz5
module dz5 (
  input  [7:0] in_1,
  input  [3:0] in_2,
  input  in_3,
  input  in_4,
  input  [7:0] in_5,
  input  in_6,
  input  in_7,
  output [7:0] out_8,
  output [7:0] out_9
);

  REG8 reg8_1 (.I(out_9), .LD(in_6), .CLK(in_7), .A(in_5));  // open: Cout, Eout, CL, SL, IL, SR, IR, DEC, INC
  MEM16x8 mem16x8_1 (.DOUT(out_8), .WR_RD(in_3), .A(in_2), .CS(1'b1), .CLK(in_4), .DIN(in_1));
endmodule

module Chips (
  input  init,
  input  calc,
  input  [7:0] stake,
  input  [7:0] even_odd,
  input  [7:0] straight_up,
  input  rst,
  input  clk,
  output [7:0] gain,
  output [7:0] chipsy
);

  wire and_1_out, or_1_out;
  wire [7:0] multiplexer_1_out, reg8_1_i, subtractor_1_out;

  or or_1 (or_1_out, init, calc);
  and and_1 (and_1_out, or_1_out, ~rst);  // AND_Gate
  REG8 reg8_1 (
    .I(reg8_1_i), .CL(rst), .LD(and_1_out), .CLK(clk), .A(multiplexer_1_out));  // open: Cout, Eout, SL, IL, SR, IR, DEC, INC
  Adder adder_1 (.a(even_odd), .b(straight_up), .out(gain));  // open: cin, cout
  Subtractor subtractor_1 (.a(stake), .b(reg8_1_i), .out(subtractor_1_out));  // open: bin, bout
  Multiplexer #(.enable("false"), .width(8)) multiplexer_1 (
    .in0(chipsy), .in1(8'h64), .out(multiplexer_1_out), .sel(init));
  Adder adder_2 (.a(gain), .b(subtractor_1_out), .out(chipsy));  // open: cin, cout
endmodule

module Timer (
  input  start,
  input  rst,
  input  clk,
  output out1
);

  wire and_1_out, d_ff_1_q, risingedge_1_out1;
  wire [2:0] prandom07_1_z2;
  wire [7:0] reg8_1_i;

  RisingEdge risingedge_1 (.in1(start), .clk(clk), .out1(risingedge_1_out1));
  PRandom07 prandom07_1 (
    .rst(rst), .nxt(risingedge_1_out1), .clk(clk), .z2(prandom07_1_z2[0]), .z1(prandom07_1_z2[1]),
    .z0(prandom07_1_z2[2]));
  REG8 reg8_1 (
    .I(reg8_1_i), .CL(rst), .LD(and_1_out), .INC(out1), .CLK(clk), .A({{5{1'b0}}, prandom07_1_z2}));  // open: Cout, Eout, SL, IL, SR, IR, DEC
  D_Flip_Flop d_ff_1 (.D(risingedge_1_out1), .clk(clk), .Q(d_ff_1_q));  // open: Qn, preset, reset
  and and_1 (and_1_out, ~rst, d_ff_1_q, ~out1);  // AND_Gate
  or or_1 (out1, reg8_1_i[2], reg8_1_i[1], reg8_1_i[0]);
endmodule

module MeanGainCtrl (
  input  [7:0] gain,
  input  wr,
  input  mean,
  input  rst,
  input  clk,
  output [7:0] out_6
);

  wire and_1_out, and_2_out, and_3_out, and_4_out, and_5_out, meangain_1_addrrd0, meangain_1_cout, or_1_out,
       or_2_out, or_3_out, or_4_out, or_5_out, or_6_out, or_7_out, T0_out, T1_out, T2_out, T3_out, T4_out,
       T5_out, T6_out, t_ff_1_q, t_ff_1_qn, t_ff_2_q, t_ff_2_qn, t_ff_3_q, t_ff_3_qn, t_ff_4_q, t_ff_4_qn;

  or or_1 (or_1_out, T2_out, T4_out, T5_out);
  or or_2 (or_2_out, T3_out, T4_out, T5_out);
  or or_3 (or_3_out, T3_out, T5_out);
  MeanGain meangain_1 (
    .gain(gain), .wr(wr), .mean(mean), .rst(rst), .clk(clk), .clAddrRd(1'b0), .decAddrRd(T1_out), .S1(1'b0),
    .S0(1'b1), .Cin(1'b0), .ldL0(or_1_out), .clL0(T0_out), .ldL1(or_2_out), .clL1(T0_out), .rdALU(or_3_out),
    .ldRes(T6_out), .clRes(1'b0), .rdS(T6_out), .rdMem(T2_out), .rdConst(T4_out), .rdRes(1'b0), .ldS(T3_out),
    .clS(T0_out), .srS(T5_out), .RES(out_6), .addrRd0(meangain_1_addrrd0), .Cout(meangain_1_cout));
  and and_1 (and_1_out, T0_out, mean, ~meangain_1_addrrd0);  // AND_Gate
  and and_2 (and_2_out, T3_out, ~meangain_1_addrrd0);  // AND_Gate
  and and_3 (and_3_out, T5_out, ~meangain_1_cout);  // AND_Gate
  and and_4 (and_4_out, T0_out, mean, meangain_1_addrrd0);
  and and_5 (and_5_out, T3_out, meangain_1_addrrd0);
  T_Flip_Flop t_ff_1 (.T(or_4_out), .clk(clk), .Q(t_ff_1_q), .Qn(t_ff_1_qn));  // open: reset, preset
  or or_4 (or_4_out, T4_out, T6_out);
  T_Flip_Flop t_ff_2 (.T(or_5_out), .clk(clk), .Q(t_ff_2_q), .Qn(t_ff_2_qn));  // open: reset, preset
  or or_5 (or_5_out, T2_out, T3_out);
  T_Flip_Flop t_ff_3 (.T(or_6_out), .clk(clk), .Q(t_ff_3_q), .Qn(t_ff_3_qn));  // open: reset, preset
  or or_6 (or_6_out, and_1_out, T1_out, and_2_out, and_3_out);
  T_Flip_Flop t_ff_4 (.T(or_7_out), .clk(clk), .Q(t_ff_4_q), .Qn(t_ff_4_qn));  // open: reset, preset
  or or_7 (or_7_out, and_4_out, and_5_out);
  and T0 (T0_out, t_ff_1_qn, t_ff_2_qn, t_ff_3_qn, t_ff_4_qn);
  and T1 (T1_out, t_ff_1_qn, t_ff_2_qn, t_ff_3_qn, t_ff_4_q);
  and T2 (T2_out, t_ff_1_qn, t_ff_2_qn, t_ff_3_q, t_ff_4_q);
  and T3 (T3_out, t_ff_1_qn, t_ff_2_q, t_ff_3_q, t_ff_4_q);
  and T4 (T4_out, t_ff_1_qn, t_ff_2_qn, t_ff_3_q, t_ff_4_qn);
  and T5 (T5_out, t_ff_1_q, t_ff_2_qn, t_ff_3_q, t_ff_4_qn);
  and T6 (T6_out, t_ff_1_q, t_ff_2_qn, t_ff_3_qn, t_ff_4_qn);
endmodule
